# Fritzing sketch CircuitDesign (saved by Fritzing 0.9.10b)

parts:
  Mod1 = Raspberry Pi 4B
  WATER_PUMP1 = water pump/motor
  KY-1 = Keyes Relay [package=THT]
  Load_Cell2 = Load Cell - Red/white/black/green
  Part2 = HX711 Weighing Sensor Module
  Part3 = Arduino Nano (Rev3.0)
  Squix2 = OLED 0.96" 128x64 I2C SSD1306
  SPKR1 = Loudspeaker  # not connected
  U2 = TCM8240MD [package=tcm8240md]  # not connected

nets:
  3V3: Mod1.3V3, Squix2.VCC
  N1: Mod1.GPIO2, Squix2.SCA
  N2: Mod1.GPIO3, Squix2.SCL
  GND: Mod1.GND, Squix2.GND
  GND_2: WATER_PUMP1.pin_1, KY-1.ground, Part2.GND, Part3.GND
  N3: WATER_PUMP1.pin_2, KY-1.NO
  N4: KY-1.signal, Part3.D8
  VCC: KY-1.power, KY-1.C, Part2.VCC, Part3.5V
  N5: Load_Cell2.wire1, Part2.E+
  N6: Load_Cell2.wire2, Part2.A-
  N7: Load_Cell2.wire3, Part2.E-
  N8: Load_Cell2.wire4, Part2.A+
  N9: Part2.DO/RX, Part3.D7
  N10: Part2.CK/TX, Part3.D5

notes:
  Wired Speaker Jack

custom parts:
  water pump/motor: WATER PUMP BY ARDUBLOCKTR
  Keyes Relay: The Keyes 5V relay module is suitable for SCM development, home appliance control. It uses a 5V~12V TIL control signal which can control DC / AC signal.
  Load Cell - Red/white/black/green: A rectangle load cell/weighting pressure Sensor with four wires - Red, white, black, green. Normally corresponding with E+, E-, A+, A- respectively.
  HX711 Weighing Sensor Module: HX711 is a precision 24-bit analog-to-digital converter (ADC) designed for weigh scales and industrial control applications to interface directly with a bridge sensor.
