# Fritzing sketch Circuit_Design_EPES_v2.0.0 (saved by Fritzing 0.9.10b)
stripboards: 3

parts:
  Touchscreen_TFT_Display_-_60mA = 2.8" SPI TFT Module [part_number=MSP2807]
  DS1 = DS18B20 1-Wire Temperature Sensor Probe
  Load_Cell3 = Load Cell - Red/white/black/green
  5v_3A = Mini-360 DC-DC Buck converter [package=THT]
  ESP32-TOUCH = DOIT Esp32 DevKit v1 (30 pins long, 11 pins width) [part_number=ESP32S-PIN30]
  RY1 = SSR-40VA
  Mod1 = Raspberry Pi 4B
  Part8 = Black Joystick KY-023
  R1 = Resistor [tolerance=±5% power=0.25 resistance=4.7k package=THT]
  Boost_to_26V = XL6009
  12v_Solenoid_Valve_10mA = Plastic Solenoid Valve
  12v_Water_Pump_1_5A = water pump/motor
  26V_LED1_1_5A = LEDs [package=fkit-led-1206]
  26V_LED2_1_5A = LEDs [package=fkit-led-1206]
  12v_10A_Main_Power_Supply = 2.1mm Barrel Jack with Terminal Block
  R2 = Heating Pad
  HOT_WATER = Adafruit 3104 lighted pushbutton [package=THT]
  WARM_WATER = Adafruit 3104 lighted pushbutton [package=THT]
  LOCK_TEMPERATURE = Adafruit 3104 lighted pushbutton [package=THT]
  INCREASE_TEMP = Pushbutton [package="[THT]"]
  DECREASE_TEMP = Pushbutton [package="[THT]"]
  TEMPERATURE_SOUND = Pushbutton [package="[THT]"]
  TANK_PERCENTAGE_SOUND = Pushbutton [package="[THT]"]
  74HC1 = 74HC04 - Hex Inverter [package="DIP (Dual Inline) [THT]"]
  NOT_NECESSARY = Resistor [tolerance=±5% power=0.25 resistance=10k package=THT]
  R4 = Resistor [tolerance=±5% power=0.25 resistance=10k package=THT]
  R6 = Resistor [tolerance=±5% power=0.25 resistance=10k package=THT]
  R7 = Resistor [tolerance=±5% power=0.25 resistance=10k package=THT]
  NOT_NECESSARY_2 = Resistor [tolerance=±5% power=0.25 resistance=10k package=THT]
  NOT_NECESSARY_3 = Resistor [tolerance=±5% power=0.25 resistance=10k package=THT]
  3_3v_3A = Mini-360 DC-DC Buck converter [package=THT]
  BUTTON_SWITCH = Terminal Block - 3 pins [package=THT]
  BUTTON_DATA = Terminal Block - 2 pins [package=THT]
  BUTTON_DATA_2 = Terminal Block - 2 pins [package=THT]
  BUTTON_LED = Terminal Block - 3 pins [package=THT]
  R10 = Resistor [tolerance=±5% power=0.25 resistance=220 package=THT]
  R12 = Resistor [tolerance=±5% power=0.25 resistance=220 package=THT]
  R11 = Resistor [tolerance=±5% power=0.25 resistance=220 package=THT]
  SPKR1 = Loudspeaker  # not connected
  CAMERA1 = TTL Serial JPEG Camera  # not connected
  J20 = Terminal Block - 2 pins [package=THT]
  R5 = Resistor [tolerance=±5% power=0.25 resistance=10k package=THT]
  KY-1 = Keyes Relay [package=THT]
  KY-2 = Keyes Relay [package=THT]
  J23 = Terminal Block - 2 pins [package=THT]
  J24 = Terminal Block - 2 pins [package=THT]
  J25 = Terminal Block - 3 pins [package=THT]
  ESP32-READ = DOIT Esp32 DevKit v1 (30 pins long, 11 pins width) [part_number=ESP32S-PIN30]
  J27 = Terminal Block - 2 pins [package=THT]
  TFT_Display_Only_-_60mA = 2.8" SPI TFT Module [part_number=MSP2807]
  220v_AC1 = Lilypad Battery Connect
  J31 = Terminal Block - 2 pins [package=THT]
  J34 = Terminal Block - 2 pins [package=THT]
  J36 = Terminal Block - 2 pins [package=THT]
  Load_Cell4 = Load Cell - Red/white/black/green
  J40 = female pin header, 7 pins [form="♀ (female)"]
  J42 = Terminal Block - 2 pins [package=THT]
  J41 = female pin header, 8 pins [form="♀ (female)"]
  J43 = female pin header, 8 pins [form="♀ (female)"]
  J44 = female pin header, 8 pins [form="♀ (female)"]
  U2 = Module 4 Relais 5V [package="Module 4 Relais 5V"]
  KY-3 = Keyes Relay [package=THT]
  L2 = Solenoid  # not connected
  L3 = Solenoid  # not connected
  L4 = Solenoid  # not connected
  L5 = Solenoid  # not connected
  L6 = Solenoid
  L7 = Solenoid
  F2 = Small Fan, based on Fan - Ventilador [package=THT]
  F3 = Small Fan, based on Fan - Ventilador [package=THT]
  POWER_SWITCH = SWITCH-SPST-2 [package=switch-spst-vertical]
  J45 = female pin header, 5 pins [form="♀ (female)"]
  J46 = female pin header, 5 pins [form="♀ (female)"]
  HEATER_SWITCH = SWITCH-SPST-2 [package=switch-spst-vertical]
  J48 = Terminal Block - 3 pins [package=THT]
  J49 = Terminal Block - 2 pins [package=THT]
  Part3 = HX711 Weighing Sensor Module  # not connected
  Part9 = HX711 Weighing Sensor Module
  J50 = Piezo Speaker
  J51 = female pin header, 2 pins [form="♀ (female)"]
  J52 = Piezo Speaker
  J53 = Piezo Speaker

nets:
  N1: Touchscreen_TFT_Display_-_60mA.pin1, DS1.VDD, R1.Pin_0, J25.Line_1, TFT_Display_Only_-_60mA.pin1
  GND: Touchscreen_TFT_Display_-_60mA.pin2, DS1.GND, Part8.GND, J25.Line_3, J27.Line_2, TFT_Display_Only_-_60mA.pin2, J36.Line_1, J49.Line_2, Part9.GND
  N2: Touchscreen_TFT_Display_-_60mA.pin3, ESP32-TOUCH.D15
  N3: Touchscreen_TFT_Display_-_60mA.pin4, ESP32-TOUCH.D4
  N4: Touchscreen_TFT_Display_-_60mA.pin5, ESP32-TOUCH.D2
  N5: Touchscreen_TFT_Display_-_60mA.pin8, ESP32-TOUCH.3V3
  N6: Touchscreen_TFT_Display_-_60mA.pin10, ESP32-TOUCH.D18
  N7: Touchscreen_TFT_Display_-_60mA.pin11, ESP32-TOUCH.D21
  N8: Touchscreen_TFT_Display_-_60mA.pin12, ESP32-TOUCH.D23
  N9: Touchscreen_TFT_Display_-_60mA.pin13, ESP32-TOUCH.D19
  N10: DS1.DQ, J25.Line_2
  N11: Load_Cell3.wire1, J24.Line_1
  N12: Load_Cell3.wire2, J24.Line_2
  N13: Load_Cell3.wire3, J23.Line_1
  N14: Load_Cell3.wire4, J23.Line_2
  N15: 5v_3A.IN-, Boost_to_26V.Pin_1, 12v_Solenoid_Valve_10mA.no_name_yet#2, 12v_Water_Pump_1_5A.pin_1, 12v_10A_Main_Power_Supply.NEG, 3_3v_3A.IN-, 220v_AC1.+, J41.pin2, L7.pin1, HEATER_SWITCH.P
  5V: 5v_3A.IN+, Mod1.3V3, Mod1.5V, Boost_to_26V.Pin_0, 3_3v_3A.IN+, KY-1.C, KY-2.C, J41.pin1, F2.5V, POWER_SWITCH.P
  N16: 5v_3A.OUT+, 74HC1.Vcc, J43.pin1
  N17: 5v_3A.OUT-, HOT_WATER.pin_4, 74HC1.GND, J44.pin7, J44.pin8
  N18: ESP32-TOUCH.GND, J50.pin1, J51.pin2
  N19: ESP32-TOUCH.D5, J50.pin2, J51.pin1
  N20: RY1.Pin_1, R2.pin_0
  N21: RY1.Pin_2, Mod1.GPIO4, 12v_10A_Main_Power_Supply.POS, 220v_AC1.-, POWER_SWITCH.O
  N22: RY1.Pin_3, Mod1.GPIO6
  GND_2: RY1.Pin_4, Mod1.GND, F2.GND, J52.pin1, J53.pin1
  N23: Mod1.GPIO14, BUTTON_LED.Line_1, R12.Pin_1
  N24: Mod1.GPIO15, BUTTON_LED.Line_2, R10.Pin_1
  N25: Mod1.GPIO17, J52.pin2
  N26: Mod1.GPIO18, BUTTON_LED.Line_3, R11.Pin_1
  N27: Mod1.GPIO23, BUTTON_SWITCH.Line_2
  N28: Mod1.GPIO24, BUTTON_SWITCH.Line_3
  N29: Mod1.GPIO10, BUTTON_SWITCH.Line_1
  N30: Mod1.GPIO25, BUTTON_DATA.Line_1
  N31: Mod1.GPIO11, BUTTON_DATA.Line_2
  N32: Mod1.GPIO8, BUTTON_DATA_2.Line_1
  N33: Mod1.GPIO7, BUTTON_DATA_2.Line_2
  N34: Mod1.GPIO5, J53.pin2
  N35: Mod1.GPIO13, KY-3.signal
  N36: Mod1.GPIO19, U2.IN3
  N37: Mod1.GPIO26, U2.IN4
  N38: Mod1.GPIO20, U2.IN1
  N39: Mod1.GPIO21, U2.IN2
  N40: Part8.VRy, ESP32-READ.D26, J49.Line_1
  N41: Part8.+5V, J48.Line_1
  N42: R1.Pin_1, ESP32-READ.D22
  N43: Boost_to_26V.Pin_2, 26V_LED1_1_5A.C, 26V_LED2_1_5A.C
  N44: Boost_to_26V.Pin_3, 26V_LED1_1_5A.A, 26V_LED2_1_5A.A
  N45: 12v_Solenoid_Valve_10mA.no_name_yet#1, KY-1.NC
  N46: 12v_Water_Pump_1_5A.pin_2, KY-2.NC
  N47: R2.pin_1, HEATER_SWITCH.O
  N48: HOT_WATER.pin_2, WARM_WATER.pin_2, WARM_WATER.pin_1, LOCK_TEMPERATURE.pin_2, LOCK_TEMPERATURE.pin_1, INCREASE_TEMP.Pin_1, INCREASE_TEMP.Pin_2, DECREASE_TEMP.Pin_2, TEMPERATURE_SOUND.Pin_1, TEMPERATURE_SOUND.Pin_2, TANK_PERCENTAGE_SOUND.Pin_1, TANK_PERCENTAGE_SOUND.Pin_2, 3_3v_3A.OUT+, J40.pin1, J40.pin2, J40.pin3, J40.pin4, J40.pin5, J40.pin6, J40.pin7
  N49: HOT_WATER.pin_5, WARM_WATER.pin_5, LOCK_TEMPERATURE.pin_5, NOT_NECESSARY.Pin_1, R4.Pin_0, R6.Pin_1, R7.Pin_0, NOT_NECESSARY_2.Pin_1, NOT_NECESSARY_3.Pin_0, 3_3v_3A.OUT-, R5.Pin_0, J41.pin4, J41.pin6, J41.pin8
  N50: HOT_WATER.pin_6, R12.Pin_0, J41.pin3
  N51: WARM_WATER.pin_6, R10.Pin_0, J41.pin5
  N52: LOCK_TEMPERATURE.pin_6, R11.Pin_0, J41.pin7
  N53: INCREASE_TEMP.Pin_3, INCREASE_TEMP.Pin_4, R5.Pin_1
  N54: DECREASE_TEMP.Pin_3, DECREASE_TEMP.Pin_4, R6.Pin_0
  N55: TEMPERATURE_SOUND.Pin_3, TEMPERATURE_SOUND.Pin_4, R7.Pin_1
  N56: TANK_PERCENTAGE_SOUND.Pin_3, TANK_PERCENTAGE_SOUND.Pin_4, R4.Pin_1
  N57: 74HC1.1A, 74HC1.4Y, J43.pin7, J44.pin1
  N58: 74HC1.1B, J44.pin2
  N59: 74HC1.2A, J44.pin3
  N60: 74HC1.2Y, J44.pin4
  N61: 74HC1.3A, J44.pin5
  N62: 74HC1.3Y, J44.pin6
  N63: 74HC1.4A, J43.pin6
  N64: 74HC1.5Y, 74HC1.6A, J43.pin2, J43.pin5
  N65: 74HC1.5A, J43.pin4
  N66: 74HC1.6Y, J43.pin3
  N67: J20.Line_1, KY-2.signal
  N68: J20.Line_2, KY-1.signal
  VCC: KY-1.power, KY-2.power, U2.VCC, KY-3.power, F3.5V, J45.pin1, J45.pin2, J45.pin3, J45.pin4, J45.pin5
  GND_3: KY-1.ground, KY-2.ground, U2.GND, KY-3.ground, F3.GND, J46.pin1, J46.pin2, J46.pin3, J46.pin4, J46.pin5
  N69: ESP32-READ.D15, TFT_Display_Only_-_60mA.pin3
  N70: ESP32-READ.D2, TFT_Display_Only_-_60mA.pin5
  N71: ESP32-READ.D4, TFT_Display_Only_-_60mA.pin4
  N72: ESP32-READ.D18, TFT_Display_Only_-_60mA.pin7, TFT_Display_Only_-_60mA.pin10
  N73: ESP32-READ.D19, TFT_Display_Only_-_60mA.pin13, TFT_Display_Only_-_60mA.pin14
  N74: ESP32-READ.D21, TFT_Display_Only_-_60mA.pin11
  N75: ESP32-READ.D23, TFT_Display_Only_-_60mA.pin12
  N76: ESP32-READ.D35, J42.Line_1, J48.Line_3, Part9.CK/TX
  N77: ESP32-READ.D32, J42.Line_2, J48.Line_2, Part9.DO/RX
  N78: J27.Line_1, J36.Line_2, Part9.VCC
  N79: J31.Line_1, Load_Cell4.wire3, Part9.A+
  N80: J31.Line_2, Load_Cell4.wire4, Part9.A-
  N81: J34.Line_1, Load_Cell4.wire1, Part9.E+
  N82: J34.Line_2, Load_Cell4.wire2, Part9.E-
  N83: U2.K1-NF, U2.K2-NF, U2.K3-NF, U2.K4-NF, KY-3.C, L7.pin2
  N84: KY-3.NC, L6.pin2

notes:
  12v 10A Power Supply
  26v 3A Power Supply
  220v AC

custom parts:
  2.8" SPI TFT Module: A generic 2.8 inch LCD TFT 320x240 display with touchscreen and SD card slot. Uses the ILI9341 controller, like the Adafruit displays of this size uses.
  Load Cell - Red/white/black/green: A rectangle load cell/weighting pressure Sensor with four wires - Red, white, black, green. Normally corresponding with E+, E-, A+, A- respectively.
  Mini-360 DC-DC Buck converter: Mini-360 DC-DC Buck converter. Tiny buck step down voltage converter, input voltage 4.75 to 23V output 1 to 17V adjustable. Available from ebay and the like.
  DOIT Esp32 DevKit v1 (30 pins long, 11 pins width): The DOIT Esp32 DevKit v1 is one of the development board created by DOIT to evaluate the ESP-WROOM-32 module. It is based on the ESP32 microcontroller that boasts Wifi, Bluetooth, Ethernet and Low Power support all in a single chip. (vanepp) made breadboard work, adjusted pin numbering and labels and reduced size of schematic and cleaned up pcb. This chip is 30pins long (2 x15) and 11 pins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
  SSR-40VA: SSR-40VA solid state relay.
  Black Joystick KY-023: Description: The joystick is a combination of 2 analoog potentiometer and a digital switch. Arduino GND --> Module pin - Arduino +5V --> Module pin +5V Arduino Analoog 0 --> Module VRx Arduino Analoog 1 --> Module VRy Arduino Digital --> Module SW Dimensions: 1" x 1.25"
  XL6009: XL6009 Boost Converter Module DC to DC 3.0-30V to 5-35V Output Voltage Adjustable Step Up Board.
  water pump/motor: WATER PUMP BY ARDUBLOCKTR
  Heating Pad: A thermoresistant material with an embeded conductor that dissipates electrical energy into heat.
  Adafruit 3104 lighted pushbutton: This Mini Illuminated Momentary Power Button it an adorable breadboard-friendly tactile switch that has a built-in LED. It provides a simple way to add a tactile switch and a colorful universal power symbol to your project.
  74HC04 - Hex Inverter: The 74HC/HCT04 are high-speed Si-gate CMOS devicesand are pin compatible with low power Schottky TTL(LSTTL). They are specified in compliance with JEDECstandard no. 7A. The 74HC/HCT04 provide six invertingbuffers.
  Terminal Block - 3 pins: Generic Screw Terminal 9.5mm
  Terminal Block - 2 pins: Generic Screw Terminal 9.5mm
  TTL Serial JPEG Camera: TTL Serial JPEG Camera with NTSC Out
  Keyes Relay: The Keyes 5V relay module is suitable for SCM development, home appliance control. It uses a 5V~12V TIL control signal which can control DC / AC signal.
  Module 4 Relais 5V: Module 4 Relais 5V 4x SPD-06VDC-SD-C
  Small Fan, based on Fan - Ventilador: Small 2-pin fan, commonly used with single-board computers, 3d-printers, etc. This work is based on a much larger fan, as commonly found in desktop computers
  HX711 Weighing Sensor Module: HX711 is a precision 24-bit analog-to-digital converter (ADC) designed for weigh scales and industrial control applications to interface directly with a bridge sensor.
