# Fritzing sketch Microprocessor_v1.0.0 (saved by Fritzing 0.9.10b)

parts:
  Part1 = GY-VL53L0XV2 Laser Ranger Module
  OLED1 = OLED 128x64 I2C Monochrome Display VDD-GND
  Part3 = HX711 Weighing Sensor Module
  Load_Cell1 = Load Cell - Red/white/black/green
  KY-1 = Keyes Relay [package=THT]
  WATER_PUMP1 = water pump/motor
  J1 = 2.1mm Barrel Jack with Terminal Block
  Part4 = Arduino Uno (Rev3)
  Mod1 = Raspberry Pi 4B
  LED1 = LEDs [package=led-1206]
  KY-2 = Keyes Relay [package=THT]
  SPKR1 = Loudspeaker  # not connected
  S1 = Square Pushbutton
  S2 = Square Pushbutton

nets:
  VCC: Part1.VCC, Mod1.3V3
  GND: Part1.GND, KY-1.signal, KY-1.ground, Mod1.GND, Mod1.GPIO17, KY-2.ground
  N1: Part1.SCL, Mod1.GPIO3
  N2: Part1.SDA, Mod1.GPIO2
  VDD: OLED1.VDD, Part3.VCC, Part4.5V, S1.leg0, S2.leg0
  GND_2: OLED1.GND, Part3.GND, Part4.GND
  N3: OLED1.SCK, Part4.A5/SCL
  N4: OLED1.SDA, Part4.A4/SDA
  N5: Part3.DO/RX, Part4.A0
  N6: Part3.CK/TX, Part4.A1
  N7: Part3.E+, Load_Cell1.wire1
  N8: Part3.E-, Load_Cell1.wire3
  N9: Part3.A+, Load_Cell1.wire2
  N10: Part3.A-, Load_Cell1.wire4
  N11: KY-1.power, Mod1.5V, KY-2.power
  N12: KY-1.C, J1.POS, KY-2.C
  N13: KY-1.NO, WATER_PUMP1.pin_2
  N14: WATER_PUMP1.pin_1, J1.NEG, LED1.C
  N15: Mod1.GPIO18, S1.leg1
  N16: Mod1.GPIO27, S2.leg1
  N17: Mod1.GPIO25, KY-2.signal
  N18: LED1.A, KY-2.NC

notes:
  USB
  ⚠️12v 4.1A 50W
  ⚠️12v 0.7A
  VL53L0X LiDAR Sensor
  5v Relay Module
  LED LIGHT
  DC JACK BARREL
  12V WATER PUMP
  20KG LOAD CELL
  HX711 ADC AMP
  OLED DISPLAY 128X64 I2C
  SPEAKER
  CAMERA
  ARDUINO UNO
  RASPBERRY PI 4B
  dispense switch
  mode switch

custom parts:
  GY-VL53L0XV2 Laser Ranger Module: The GY-VL53L0XV2 is based on the VL53L0X from ST Microelectronics, a time-of-flight ranging system integrated into a compact module.
  OLED 128x64 I2C Monochrome Display VDD-GND: OLED 128x64 I2C Monochrome Display. Note: there are two variants of this part, this one is the VDD GND SCK SDA variant. The other is GND VDD SCK SDA. Make sure you select the part that matches your module as using the incorrect part will probably destroy your module! In addition the mounting holes are marked on silkscreen but not by default drilled. If you want drilled mounting holes, copy a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
  HX711 Weighing Sensor Module: HX711 is a precision 24-bit analog-to-digital converter (ADC) designed for weigh scales and industrial control applications to interface directly with a bridge sensor.
  Load Cell - Red/white/black/green: A rectangle load cell/weighting pressure Sensor with four wires - Red, white, black, green. Normally corresponding with E+, E-, A+, A- respectively.
  Keyes Relay: The Keyes 5V relay module is suitable for SCM development, home appliance control. It uses a 5V~12V TIL control signal which can control DC / AC signal.
  water pump/motor: WATER PUMP BY ARDUBLOCKTR
