# Fritzing sketch VL53L0X-OLED (saved by Fritzing 0.9.10b)

parts:
  Part1 = GY-VL53L0XV2 Laser Ranger Module
  OLED1 = OLED 128x64 I2C Monochrome Display VDD-GND
  Part2 = Arduino Uno (Rev3) - ICSP

nets:
  VCC: Part1.VCC, OLED1.VDD, Part2.5V
  GND: Part1.GND, OLED1.GND, Part2.GND
  N1: Part1.SCL, OLED1.SCK, Part2.A5/SCL
  N2: Part1.SDA, OLED1.SDA, Part2.A4/SDA

custom parts:
  GY-VL53L0XV2 Laser Ranger Module: The GY-VL53L0XV2 is based on the VL53L0X from ST Microelectronics, a time-of-flight ranging system integrated into a compact module.
  OLED 128x64 I2C Monochrome Display VDD-GND: OLED 128x64 I2C Monochrome Display. Note: there are two variants of this part, this one is the VDD GND SCK SDA variant. The other is GND VDD SCK SDA. Make sure you select the part that matches your module as using the incorrect part will probably destroy your module! In addition the mounting holes are marked on silkscreen but not by default drilled. If you want drilled mounting holes, copy a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
