# Fritzing sketch Water Pumping (saved by Fritzing 0.9.10b)
breadboards: 1

parts:
  WATER_PUMP1 = water pump/motor
  KY-1 = Keyes Relay [package=THT]
  Part4 = Arduino Uno (Rev3)
  R1 = Resistor [tolerance=±5% power=0.25 resistance=10k package=THT]
  S1 = Pushbutton [package="[THT]"]

nets:
  N1: WATER_PUMP1.pin_1, KY-1.ground, Part4.GND, R1.Pin_0
  N2: WATER_PUMP1.pin_2, KY-1.NO
  N3: KY-1.signal, Part4.D3_PWM
  N4: KY-1.power, KY-1.C, Part4.5V, S1.Pin_1, S1.Pin_2
  N5: Part4.D2, R1.Pin_1, S1.Pin_3, S1.Pin_4

custom parts:
  water pump/motor: WATER PUMP BY ARDUBLOCKTR
  Keyes Relay: The Keyes 5V relay module is suitable for SCM development, home appliance control. It uses a 5V~12V TIL control signal which can control DC / AC signal.
