# Fritzing sketch Weight Sensor (saved by Fritzing 0.9.10b)

parts:
  Load_Cell2 = Load Cell - Red/white/black/green
  Part2 = HX711 Weighing Sensor Module
  Part4 = Arduino Uno (Rev3)

nets:
  N1: Load_Cell2.wire1, Part2.E+
  N2: Load_Cell2.wire2, Part2.A+
  N3: Load_Cell2.wire3, Part2.E-
  N4: Load_Cell2.wire4, Part2.A-
  VCC: Part2.VCC, Part4.5V
  GND: Part2.GND, Part4.GND
  N5: Part2.DO/RX, Part4.A0
  N6: Part2.CK/TX, Part4.A1

custom parts:
  Load Cell - Red/white/black/green: A rectangle load cell/weighting pressure Sensor with four wires - Red, white, black, green. Normally corresponding with E+, E-, A+, A- respectively.
  HX711 Weighing Sensor Module: HX711 is a precision 24-bit analog-to-digital converter (ADC) designed for weigh scales and industrial control applications to interface directly with a bridge sensor.
